// Logisim project 7 Seg Dis.circ as structural Verilog: 1 circuit, main circuit main
module main (
  input  in_1,
  input  in_2,
  input  in_3,
  input  in_4,
  input  in_5,
  input  in_6,
  input  in_7
);

  wire dip_74247_1_p11, dip_74247_1_p12, dip_74247_1_p13, dip_74247_1_p14, dip_74247_1_p15, dip_74247_1_p16,
       dip_74247_1_p17;

  // DIP_74247 dip_74247_1: pin names not known; wires that end beside it: in_2, in_3, in_4, in_2, in_3, in_6, in_5, in_7, in_4, in_1, dip_74247_1_p11, dip_74247_1_p12, dip_74247_1_p13, dip_74247_1_p14, dip_74247_1_p15, dip_74247_1_p16, dip_74247_1_p17
  _7_Segment_Display u_7_segment_display_1 (
    .g(dip_74247_1_p11), .f(dip_74247_1_p12), .a(dip_74247_1_p13), .b(dip_74247_1_p14), .e(dip_74247_1_p17),
    .d(dip_74247_1_p16), .c(dip_74247_1_p15));  // open: dp
endmodule
