// Logisim project 7A.circ as structural Verilog: 1 circuit, main circuit main
module main (
  input  in_1,
  output Y,
  output A,
  output B
);

  wire and_1_out, clock_1_out, not_1_out, not_2_out, xor_1_out;

  Clock clock_1 (.out(clock_1_out));
  D_Flip_Flop d_ff_1 (.clk(clock_1_out), .D(xor_1_out), .Q(A));  // open: Qn, preset, en, reset
  xor xor_1 (xor_1_out, in_1, A);
  not not_1 (not_1_out, in_1);
  not not_2 (not_2_out, A);
  and and_1 (and_1_out, not_1_out, not_2_out);
  and and_2 (Y, in_1, not_2_out);
  D_Flip_Flop d_ff_2 (.clk(clock_1_out), .D(and_1_out), .Q(B));  // open: Qn, preset, en, reset
endmodule
