// Logisim project MUX Fuad.circ as structural Verilog: 1 circuit, main circuit main
module main (
  input  _1,
  input  _0,
  input  D,
  input  [3:0] in_4,
  output out_5
);

  Multiplexer #(.select(4)) multiplexer_1 (
    .in0(_1), .in1(_1), .in2(D), .in3(D), .in4(D), .in5(D), .in6(_0), .in7(_0), .in8(_1), .in9(_1),
    .in10(_0), .in11(_0), .in12(_0), .in13(_0), .in14(_1), .in15(_1), .out(out_5), .sel(in_4), .en(_1));
endmodule
