// Logisim project MUX with basic gates.circ as structural Verilog: 1 circuit, main circuit main
module main (
  input  _1,
  input  A,
  input  B,
  input  C,
  output out_5
);

  wire and_1_out, and_2_out, and_3_out, and_4_out, not_1_out, not_2_out, not_3_out, or_1_out, or_2_out;

  not not_1 (not_1_out, _1);
  not not_2 (not_2_out, A);
  not not_3 (not_3_out, B);
  and and_1 (and_1_out, not_1_out, not_2_out, not_3_out);
  and and_2 (and_2_out, _1, not_2_out, B);
  and and_3 (and_3_out, C, A, not_3_out);
  and and_4 (and_4_out, C, A, B);
  or or_1 (or_1_out, and_1_out, and_2_out);
  or or_2 (or_2_out, and_3_out, and_4_out);
  or or_3 (out_5, or_1_out, or_2_out);

  // Notes on the sheet:
  //   0
endmodule
