// Logisim project Project Decoder.circ as structural Verilog: 1 circuit, main circuit main
module main (
);

  wire and_1_out, and_2_out, clock_1_out, decoder_1_out0, decoder_1_out1, decoder_1_out2, decoder_1_out3,
       decoder_1_out4, decoder_1_out5, decoder_1_out6, decoder_1_out7, decoder_1_out8, j_k_ff_4_qn, or_1_out,
       or_2_out, or_3_out, or_4_out, or_5_out, or_6_out, or_7_out, or_8_out, or_9_out;
  wire [3:0] j_k_ff_1_q;

  Clock clock_1 (.out(clock_1_out));
  Decoder #(.select(4)) decoder_1 (
    .out0(decoder_1_out0), .out1(decoder_1_out1), .out2(decoder_1_out2), .out3(decoder_1_out3),
    .out4(decoder_1_out4), .out5(decoder_1_out5), .out6(decoder_1_out6), .out7(decoder_1_out7),
    .out8(decoder_1_out8), .sel(j_k_ff_1_q), .en(1'b1));  // open: out9, out10, out11, out12, out13, out14, out15
  J_K_Flip_Flop j_k_ff_1 (
    .J(j_k_ff_4_qn), .clk(clock_1_out), .K(1'b1), .Q(j_k_ff_1_q[0]));  // open: Qn, preset, en, reset
  and and_1 (and_1_out, j_k_ff_1_q[0], j_k_ff_1_q[1]);
  J_K_Flip_Flop j_k_ff_2 (
    .J(j_k_ff_1_q[0]), .clk(clock_1_out), .K(j_k_ff_1_q[0]), .Q(j_k_ff_1_q[1]));  // open: Qn, preset, en, reset
  or or_1 (or_1_out, decoder_1_out0, decoder_1_out1, decoder_1_out2);
  J_K_Flip_Flop j_k_ff_3 (
    .J(and_1_out), .clk(clock_1_out), .K(and_1_out), .Q(j_k_ff_1_q[2]));  // open: Qn, preset, en, reset
  or or_2 (or_2_out, or_1_out, decoder_1_out6, decoder_1_out8);
  and and_2 (and_2_out, and_1_out, j_k_ff_1_q[2]);
  or or_3 (or_3_out, decoder_1_out0, decoder_1_out1, decoder_1_out2, decoder_1_out3, decoder_1_out5);
  or or_4 (or_4_out, decoder_1_out1, decoder_1_out6, decoder_1_out7, decoder_1_out8);
  or or_5 (or_5_out, or_1_out, decoder_1_out4, decoder_1_out6, decoder_1_out7, decoder_1_out8);
  J_K_Flip_Flop j_k_ff_4 (
    .J(and_2_out), .clk(clock_1_out), .K(1'b1), .Q(j_k_ff_1_q[3]), .Qn(j_k_ff_4_qn));  // open: preset, en, reset
  or or_6 (or_6_out, decoder_1_out0, decoder_1_out6, decoder_1_out8, decoder_1_out7);
  or or_7 (or_7_out, decoder_1_out0, decoder_1_out2, decoder_1_out3, decoder_1_out5, decoder_1_out6);
  or or_8 (or_8_out, or_3_out, decoder_1_out8, decoder_1_out6, decoder_1_out7);
  or or_9 (or_9_out, or_7_out, decoder_1_out7, decoder_1_out8);
  _7_Segment_Display u_7_segment_display_1 (
    .g(or_5_out), .f(or_2_out), .a(or_6_out), .b(or_9_out), .e(or_1_out), .d(or_4_out), .c(or_8_out));  // open: dp
endmodule
