// Logisim project Project MUX.circ as structural Verilog: 1 circuit, main circuit main
module main (
);

  wire and_1_out, and_2_out, clock_1_out, j_k_ff_4_qn, multiplexer_1_out, multiplexer_2_out,
       multiplexer_3_out, multiplexer_4_out, multiplexer_5_out, multiplexer_6_out, multiplexer_7_out;
  wire [3:0] j_k_ff_1_q;

  Clock clock_1 (.out(clock_1_out));
  J_K_Flip_Flop j_k_ff_1 (
    .J(j_k_ff_4_qn), .clk(clock_1_out), .K(1'b1), .Q(j_k_ff_1_q[0]));  // open: Qn, preset, en, reset
  Multiplexer #(.select(4)) multiplexer_1 (
    .in0(1'b1), .in1(1'b0), .in2(1'b0), .in3(1'b0), .in4(1'b0), .in5(1'b0), .in6(1'b1), .in7(1'b1),
    .in8(1'b1), .out(multiplexer_1_out), .sel(j_k_ff_1_q), .en(1'b1));  // open: in9, in10, in11, in12, in13, in14, in15
  Multiplexer #(.select(4)) multiplexer_2 (
    .in0(1'b1), .in1(1'b0), .in2(1'b1), .in3(1'b1), .in4(1'b0), .in5(1'b1), .in6(1'b1), .in7(1'b1),
    .in8(1'b1), .out(multiplexer_2_out), .sel(j_k_ff_1_q), .en(1'b1));  // open: in9, in10, in11, in12, in13, in14, in15
  Multiplexer #(.select(4)) multiplexer_3 (
    .in0(1'b1), .in1(1'b1), .in2(1'b1), .in3(1'b1), .in4(1'b0), .in5(1'b1), .in6(1'b1), .in7(1'b1),
    .in8(1'b1), .out(multiplexer_3_out), .sel(j_k_ff_1_q), .en(1'b1));  // open: in9, in10, in11, in12, in13, in14, in15
  Multiplexer #(.select(4)) multiplexer_4 (
    .in0(1'b0), .in1(1'b1), .in2(1'b0), .in3(1'b0), .in4(1'b0), .in5(1'b0), .in6(1'b1), .in7(1'b1),
    .in8(1'b1), .out(multiplexer_4_out), .sel(j_k_ff_1_q), .en(1'b1));  // open: in9, in10, in11, in12, in13, in14, in15
  and and_1 (and_1_out, j_k_ff_1_q[0], j_k_ff_1_q[1]);
  J_K_Flip_Flop j_k_ff_2 (
    .J(j_k_ff_1_q[0]), .clk(clock_1_out), .K(j_k_ff_1_q[0]), .Q(j_k_ff_1_q[1]));  // open: Qn, preset, en, reset
  J_K_Flip_Flop j_k_ff_3 (
    .J(and_1_out), .clk(clock_1_out), .K(and_1_out), .Q(j_k_ff_1_q[2]));  // open: Qn, preset, en, reset
  _7_Segment_Display u_7_segment_display_1 (
    .g(multiplexer_7_out), .f(multiplexer_6_out), .a(multiplexer_1_out), .b(multiplexer_2_out),
    .e(multiplexer_5_out), .d(multiplexer_4_out), .c(multiplexer_3_out));  // open: dp
  and and_2 (and_2_out, and_1_out, j_k_ff_1_q[2]);
  J_K_Flip_Flop j_k_ff_4 (
    .J(and_2_out), .clk(clock_1_out), .K(1'b1), .Q(j_k_ff_1_q[3]), .Qn(j_k_ff_4_qn));  // open: preset, en, reset
  Multiplexer #(.select(4)) multiplexer_5 (
    .in0(1'b1), .in1(1'b1), .in2(1'b1), .in3(1'b0), .in4(1'b0), .in5(1'b0), .in6(1'b0), .in7(1'b0),
    .in8(1'b0), .out(multiplexer_5_out), .sel(j_k_ff_1_q), .en(1'b1));  // open: in9, in10, in11, in12, in13, in14, in15
  Multiplexer #(.select(4)) multiplexer_6 (
    .in0(1'b1), .in1(1'b1), .in2(1'b1), .in3(1'b0), .in4(1'b0), .in5(1'b0), .in6(1'b1), .in7(1'b0),
    .in8(1'b1), .out(multiplexer_6_out), .sel(j_k_ff_1_q), .en(1'b1));  // open: in9, in10, in11, in12, in13, in14, in15
  Multiplexer #(.select(4)) multiplexer_7 (
    .in0(1'b1), .in1(1'b1), .in2(1'b1), .in3(1'b0), .in4(1'b1), .in5(1'b0), .in6(1'b1), .in7(1'b1),
    .in8(1'b1), .out(multiplexer_7_out), .sel(j_k_ff_1_q), .en(1'b1));  // open: in9, in10, in11, in12, in13, in14, in15

  // Notes on the sheet:
  //   a
  //   b
  //   c
  //   d
  //   e
  //   f
  //   g
endmodule
