// Logisim project Project NAND.circ as structural Verilog: 1 circuit, main circuit main
module main (
);

  wire and_1_out, and_2_out, clock_1_out, j_k_ff_1_q, j_k_ff_2_q, j_k_ff_3_q, j_k_ff_4_q, j_k_ff_4_qn,
       nand_1_out, nand_2_out, nand_3_out, nand_4_out, nand_5_out, nand_6_out, nand_7_out, nand_8_out,
       nand_9_out, nand_10_out, nand_11_out, nand_12_out, nand_13_out, nand_14_out, nand_15_out, nand_16_out,
       nand_17_out, nand_18_out, nand_19_out, nand_20_out, nand_21_out, nand_22_out, nand_23_out,
       nand_24_out, nand_25_out, nand_26_out, nand_27_out, nand_28_out, nand_29_out, nand_30_out,
       nand_31_out, nand_32_out, nand_33_out, nand_34_out, nand_35_out, nand_36_out;

  Clock clock_1 (.out(clock_1_out));
  J_K_Flip_Flop j_k_ff_1 (.J(j_k_ff_4_qn), .clk(clock_1_out), .K(1'b1), .Q(j_k_ff_1_q));  // open: Qn, preset, en, reset
  nand nand_1 (nand_1_out, j_k_ff_4_q, j_k_ff_4_q);
  J_K_Flip_Flop j_k_ff_2 (
    .J(j_k_ff_1_q), .clk(clock_1_out), .K(j_k_ff_1_q), .Q(j_k_ff_2_q));  // open: Qn, preset, en, reset
  and and_1 (and_1_out, j_k_ff_1_q, j_k_ff_2_q);
  nand nand_2 (nand_2_out, j_k_ff_3_q, j_k_ff_3_q);
  J_K_Flip_Flop j_k_ff_3 (
    .J(and_1_out), .clk(clock_1_out), .K(and_1_out), .Q(j_k_ff_3_q));  // open: Qn, preset, en, reset
  and and_2 (and_2_out, and_1_out, j_k_ff_3_q);
  nand nand_3 (nand_3_out, j_k_ff_2_q, j_k_ff_2_q);
  J_K_Flip_Flop j_k_ff_4 (
    .J(and_2_out), .clk(clock_1_out), .K(1'b1), .Q(j_k_ff_4_q), .Qn(j_k_ff_4_qn));  // open: preset, en, reset
  nand nand_4 (nand_4_out, j_k_ff_1_q, j_k_ff_1_q);
  nand nand_5 (nand_5_out, j_k_ff_3_q, j_k_ff_2_q);
  nand nand_6 (nand_6_out, nand_2_out, nand_3_out);
  nand nand_7 (nand_7_out, nand_2_out, nand_4_out);
  nand nand_8 (nand_8_out, j_k_ff_3_q, j_k_ff_1_q);
  nand nand_9 (nand_9_out, j_k_ff_3_q, nand_4_out);
  nand nand_10 (nand_10_out, nand_2_out, nand_3_out);
  nand nand_11 (nand_11_out, nand_1_out, nand_2_out);
  nand nand_12 (nand_12_out, nand_1_out, nand_2_out);
  nand nand_13 (nand_13_out, nand_2_out, nand_3_out);
  nand nand_14 (nand_14_out, j_k_ff_2_q, nand_4_out);
  nand nand_15 (nand_15_out, nand_6_out, nand_6_out);
  nand nand_16 (nand_16_out, nand_7_out, nand_8_out);
  nand nand_17 (nand_17_out, nand_9_out, nand_9_out);
  nand nand_18 (nand_18_out, nand_10_out, nand_10_out);
  nand nand_19 (nand_19_out, nand_11_out, nand_11_out);
  nand nand_20 (nand_20_out, nand_12_out, nand_12_out);
  nand nand_21 (nand_21_out, nand_13_out, nand_14_out);
  nand nand_22 (nand_22_out, nand_13_out, j_k_ff_1_q);
  nand nand_23 (nand_23_out, nand_15_out, nand_4_out);
  nand nand_24 (nand_24_out, nand_17_out, nand_3_out);
  nand nand_25 (nand_25_out, nand_18_out, j_k_ff_1_q);
  nand nand_26 (nand_26_out, nand_19_out, nand_3_out);
  nand nand_27 (nand_27_out, nand_20_out, nand_4_out);
  nand nand_28 (nand_28_out, nand_22_out, nand_22_out);
  nand nand_29 (nand_29_out, nand_5_out, nand_23_out);
  nand nand_30 (nand_30_out, nand_16_out, nand_16_out);
  nand nand_31 (nand_31_out, nand_5_out, nand_25_out);
  nand nand_32 (nand_32_out, nand_31_out, nand_31_out);
  nand nand_33 (nand_33_out, nand_26_out, nand_27_out);
  nand nand_34 (nand_34_out, nand_28_out, nand_5_out);
  nand nand_35 (nand_35_out, nand_30_out, nand_3_out);
  nand nand_36 (nand_36_out, nand_32_out, nand_1_out);
  _7_Segment_Display u_7_segment_display_1 (
    .g(nand_34_out), .f(nand_21_out), .a(nand_29_out), .b(nand_35_out), .e(nand_33_out), .d(nand_36_out),
    .c(nand_24_out));  // open: dp
endmodule
