// Logisim project ff.circ as structural Verilog: 1 circuit, main circuit main
module main (
  input  B_prime,
  input  F1,
  input  F0
);

  wire and_1_out, and_2_out, and_3_out, and_4_out, not_1_out, not_2_out, or_1_out;

  not not_1 (not_1_out, F1);
  not not_2 (not_2_out, F0);
  and and_1 (and_1_out, B_prime, not_1_out, not_2_out);
  and and_2 (and_2_out, F1, F0);
  and and_3 (and_3_out, not_2_out, not_1_out);
  and and_4 (and_4_out, not_2_out, F1);
  or or_1 (or_1_out, and_1_out, and_2_out);

  // Notes on the sheet:
  //   F0'F1'
  //   F1'F0
  //   B'F1'F0'+F1F0
endmodule
