// Logisim project m.circ as structural Verilog: 1 circuit, main circuit main
module main (
  input  R,
  input  S,
  output q,
  output q_prime
);

  nor nor_1 (q, R, q_prime);
  nor nor_2 (q_prime, q, S);
endmodule
